# Fritzing sketch on,off (saved by Fritzing 0.9.4)
breadboards: 1

parts:
  Part1 = Arduino Uno (Rev3)
  LED1 = LED - 5mm [color="Green (560nm)" package="5 mm [THT]"]

nets:
  N1: Part1.D13/SCK, LED1.cathode
  N2: Part1.GND, LED1.anode
